# Fritzing sketch imu (saved by Fritzing 1.0.0rc)
breadboards: 1

parts:
  Part1 = Adafruit HUZZAH32 ESP32 Feather [part_number="Adafruit #3405"]
  Part2 = 9-DOF Absolute Orientation IMU Fusion Breakout - BNO055

nets:
  GND: Part1.GND, Part2.GND
  3.3V: Part1.3.3V, Part2.3.3V
  N1: Part1.SCL, Part2.SCL_5V
  N2: Part1.SDA, Part2.SDA_5V

custom parts:
  9-DOF Absolute Orientation IMU Fusion Breakout - BNO055: A MEMS accelerometer, magnetometer and gyroscope on a single die with a high speed ARM Cortex-M0 based processor to digest all the sensor data, abstract the sensor fusion and real time requirements away, and spit out data you can use in quaternions, Euler angles or vectors.
