# Fritzing sketch led (saved by Fritzing 0.9.9b)
breadboards: 1

parts:
  Part9 = Adafruit HUZZAH32 ESP32 Feather [part_number="Adafruit #3405"]
  LED1 = smd LED [color="Red (633nm)" package="1206 [SMD]"]
  R1 = Resistor [tolerance=±5% resistance=100 package="0805 [SMD]"]

nets:
  N1: Part9.IO21, R1.Pin_1
  N2: Part9.GND, LED1.cathode
  N3: LED1.anode, R1.Pin_0
