# Fritzing sketch motion (saved by Fritzing 0.9.9b)
breadboards: 1

parts:
  Part4 = Adafruit HUZZAH32 ESP32 Feather [part_number="Adafruit #3405"]
  SONAR1 = Maxbotix MaxSonar Ultrasonic Sensor

nets:
  N1: Part4.A2_I34, SONAR1.AN
  GND: Part4.GND, SONAR1.GND
  3.3V: Part4.3.3V, SONAR1.+5V

custom parts:
  Maxbotix MaxSonar Ultrasonic Sensor: Maxbotix MaxSonar Ultrasonic Sensor LV-EZ0, LV-EZ1, LV-EZ2, LV-EZ3, LV-EZ4
