# Fritzing sketch neopixel_individual (saved by Fritzing 1.0.0rc)
breadboards: 1

parts:
  Part1 = Adafruit HUZZAH32 ESP32 Feather [part_number="Adafruit #3405"]
  LED1 = RGB LED (com. cathode, rgb) [color="Red (633nm)" current=0.030A package="5 mm [THT]"]
  C1 = Ceramic Capacitor [capacitance=0.1µF voltage=35V package="0805 [SMD, multilayer]"]

nets:
  N1: Part1.GND, LED1.green_anode, C1.1
  N2: Part1.3.3V, LED1.common_cathode, C1.0
  N3: Part1.IO32_A7, LED1.red_anode
