# Fritzing sketch neopixel_strip (saved by Fritzing 1.0.0rc)
breadboards: 1

parts:
  Part1 = Adafruit HUZZAH32 ESP32 Feather [part_number="Adafruit #3405"]
  NEOPIXEL1 = Neopixel Strip -- Black (30/m) [part_number=1376]
  R1 = Resistor [tolerance=±5% resistance=220 package="0805 [SMD]"]

nets:
  GND: Part1.GND, NEOPIXEL1.GND
  3.3V: Part1.3.3V, NEOPIXEL1.+5V
  N1: Part1.IO32_A7, R1.Pin_0
  N2: NEOPIXEL1.Din, R1.Pin_1

custom parts:
  Neopixel Strip -- Black (30/m): These NeoPixel strips have 30 digitally-addressable pixel LEDs per meter and are very affordable and are only 12.5 mm wide, 10 mm if you remove the strip from the casing.
