# Fritzing sketch dht (saved by Fritzing 0.9.9b)
breadboards: 1

parts:
  R5 = Resistor [tolerance=±5% power=0.25 resistance=10k package=THT]
  Part3 = Adafruit HUZZAH32 ESP32 Feather [part_number="Adafruit #3405"]
  DHT1 = DHT11 Humitidy and Temperature Sensor

nets:
  N1: R5.Pin_0, Part3.IO32_A7, DHT1.DATA
  3.3V: R5.Pin_1, Part3.3.3V, DHT1.VDD
  GND: Part3.GND, DHT1.GND

custom parts:
  DHT11 Humitidy and Temperature Sensor: DHT11 Humidity and Temperature Sensor
