# Fritzing sketch fsr (saved by Fritzing 0.9.9b)
breadboards: 1

parts:
  R4 = Resistor [tolerance=±5% power=0.25 resistance=10k package=THT]
  Part2 = Adafruit HUZZAH32 ESP32 Feather [part_number="Adafruit #3405"]
  J1 = Basic Force Sensing Resistor (FSR) [package=THT]

nets:
  N1: R4.Pin_0, Part2.GND
  N2: R4.Pin_1, Part2.A2_I34, J1.pin_0
  N3: Part2.3.3V, J1.pin_1
