# Fritzing sketch mpu6050 (saved by Fritzing 0.9.9b)
breadboards: 1

parts:
  Part7 = Adafruit HUZZAH32 ESP32 Feather [part_number="Adafruit #3405"]
  Part8 = InvenSense MPU6050

nets:
  GND: Part7.GND, Part8.GND
  3.3V: Part7.3.3V, Part8.VCC
  N1: Part7.SCL, Part8.SCL
  N2: Part7.SDA, Part8.SDA
