# Fritzing sketch photo_cell (saved by Fritzing 1.0.0rc)
breadboards: 1

parts:
  R2 = Resistor [tolerance=±5% power=0.25 resistance=2.2k package=THT]
  Part1 = Adafruit HUZZAH32 ESP32 Feather [part_number="Adafruit #3405"]
  R1 = Photocell (LDR) [power=0.25W dark_resistance_@0.01lx=300kΩ light_resistance_@100lx=400Ω luminance=10lx package=THT]

nets:
  N1: R2.Pin_0, Part1.GND
  N2: R2.Pin_1, Part1.A2_I34, R1.pin_0
  N3: Part1.3.3V, R1.pin_1
