# Fritzing sketch piezo (saved by Fritzing 1.0.4)
breadboards: 1

parts:
  Part1 = Adafruit HUZZAH32 ESP32 Feather [part_number="Adafruit #3405"]
  Adafruit_STEMMA_Piezo_Driver_Amp1 = Adafruit STEMMA Piezo Driver Amp [part_number=#5791]
  J1 = Piezo Speaker

nets:
  GND: Part1.GND, Adafruit_STEMMA_Piezo_Driver_Amp1.GND
  3.3V: Part1.3.3V, Adafruit_STEMMA_Piezo_Driver_Amp1.VIN
  N1: Part1.IO27_A10, Adafruit_STEMMA_Piezo_Driver_Amp1.SIGNAL
  N2: Adafruit_STEMMA_Piezo_Driver_Amp1.VO+, J1.pin1
  N3: Adafruit_STEMMA_Piezo_Driver_Amp1.VO-, J1.pin2

custom parts:
  Adafruit STEMMA Piezo Driver Amp: Piezos make noise when you put an AC voltage across them: and the bigger the Vpp the louder they are. With your standard 3V logic microcontroller you can make 3Vpp with a PWM out, or 6Vpp differential with two complimentary outputs. But what if you want even louder? Or if you're using a piezo to sense distance using ultrasonic bounces? We found the nifty PAM8904, which is an amplifier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
