# Fritzing sketch pot (saved by Fritzing 0.9.9b)
breadboards: 1

parts:
  Part8 = Adafruit HUZZAH32 ESP32 Feather [part_number="Adafruit #3405"]
  R1 = Rotary Potentiometer (Large) [maximum_resistance=100kΩ package=THT]

nets:
  N1: Part8.A2_I34, R1.wiper
  N2: Part8.GND, R1.leg1
  N3: Part8.3.3V, R1.leg2
