# Fritzing sketch servo (saved by Fritzing 1.0.0rc)
breadboards: 1

parts:
  Part1 = Adafruit HUZZAH32 ESP32 Feather [part_number="Adafruit #3405"]
  Part2 = Adafruit PWM Servo Featherwing [part_number="Adafruit #2928"]
  J1 = Basic Servo  # not connected

nets:
  N1: Part1.IO21, Part2.G
  N2: Part1.IO17, Part2.TX
  N3: Part1.IO16, Part2.RX
  N4: Part1.MISO, Part2.MISO
  N5: Part1.MOSI, Part2.MOSI
  N6: Part1.SCK, Part2.SCK
  N7: Part1.A5_IO4, Part2.F
  N8: Part1.A4_IO36, Part2.E
  N9: Part1.A3_I39, Part2.D
  N10: Part1.A2_I34, Part2.C
  N11: Part1.A1_DAC1, Part2.B
  N12: Part1.A0_DAC2, Part2.A
  GND: Part1.GND, Part2.GND
  N13: Part1.N/C, Part2.AREF
  3.3V: Part1.3.3V, Part2.+3.3V
  N14: Part1.RESET, Part2.RESET
  N15: Part1.VBAT, Part2.VBAT
  N16: Part1.EN, Part2.EN
  N17: Part1.VBUS, Part2.USB
  N18: Part1.IO13_A12, Part2.N
  N19: Part1.IO12_A11, Part2.M
  N20: Part1.IO27_A10, Part2.L
  N21: Part1.IO33_A9, Part2.K
  N22: Part1.IO15_A8, Part2.J
  N23: Part1.IO32_A7, Part2.I
  N24: Part1.IO14_A6, Part2.H
  N25: Part1.SCL, Part2.SCL
  N26: Part1.SDA, Part2.SDA

custom parts:
  Adafruit PWM Servo Featherwing: This is the 8-Channel PWM or Servo​ FeatherWing, you can add 8 x 12-bit PWM outputs to your Feather board. You want to make a cool robot, maybe a hexapod walker, or maybe just a piece of art with a lot of moving parts. Or maybe you want to drive a lot of LEDs with precise PWM output. What now? You could give up OR you could just get our handy PWM and Servo FeatherWing. It's a lot like our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
