# Fritzing sketch tilt (saved by Fritzing 0.9.9b)
breadboards: 1

parts:
  Part7 = Adafruit HUZZAH32 ESP32 Feather [part_number="Adafruit #3405"]
  R2 = Resistor [tolerance=±5% power=0.25 resistance=10k package=THT]
  S1 = Tilt Switch [package=THT]

nets:
  N1: Part7.A2_I34, R2.Pin_1, S1.Pin_1
  N2: Part7.GND, R2.Pin_0
  N3: Part7.3.3V, S1.Pin_2
