# Fritzing sketch toggle (saved by Fritzing 1.0.0rc)
breadboards: 1

parts:
  Part7 = Adafruit HUZZAH32 ESP32 Feather [part_number="Adafruit #3405"]
  R2 = Resistor [tolerance=±5% power=0.25 resistance=10k package=THT]
  S2 = Toggle Switch [package=THT]

nets:
  N1: Part7.GND, R2.Pin_0
  N2: Part7.3.3V, S2.L2
  N3: Part7.IO12_A11, R2.Pin_1, S2.COM
